// Logisim project EP2.circ as structural Verilog: 7 circuits, main circuit teste
module teste (
  input  in_1,
  input  in_2,
  input  in_3,
  input  in_4,
  output [15:0] out_5,
  output [15:0] out_6
);

  wire clock_1_out;
  wire [7:0] pc_1_output_address;
  wire [15:0] ram_1_data;

  Clock clock_1 (.out(clock_1_out));
  PC pc_1 (.Reset(in_1), .Counter_UP(clock_1_out), .Output_Address(pc_1_output_address));  // open: Set, Input_Address
  RAM #(.dataWidth(16)) ram_1 (
    .addr(pc_1_output_address), .data(ram_1_data), .sel(in_2), .ld(in_3), .clr(in_4));  // open: clk
  IR ir_1 (
    .\Endereço (ram_1_data[7:0]), .Set(clock_1_out), .\Código (ram_1_data[15:8]), .Output(out_5));  // open: Reset
  ACC acc_1 (.Input(ram_1_data), .Output(out_6), .Set(clock_1_out));  // open: Reset
endmodule

module PC (
  input  [7:0] Input_Address,
  input  Set,
  input  Reset,
  input  Counter_UP,
  output [7:0] Output_Address
);

  wire and_1_out, and_2_out, and_3_out, and_4_out, and_5_out, and_6_out, and_7_out, and_8_out, and_9_out,
       and_10_out, and_11_out, and_12_out, and_13_out, and_14_out, and_15_out, and_16_out, j_k_ff_1_qn,
       j_k_ff_2_qn, j_k_ff_3_qn, j_k_ff_4_qn, j_k_ff_5_qn, j_k_ff_6_qn, j_k_ff_7_qn, or_1_out, or_2_out,
       or_3_out, or_4_out, or_5_out, or_6_out, or_7_out, or_8_out;

  and and_1 (and_1_out, Set, ~Input_Address[0]);  // AND_Gate
  and and_2 (and_2_out, Set, Input_Address[0]);
  or or_1 (or_1_out, Reset, and_1_out);
  J_K_Flip_Flop j_k_ff_1 (
    .J(1'b1), .clk(Counter_UP), .K(1'b1), .Q(Output_Address[0]), .Qn(j_k_ff_1_qn), .preset(and_2_out),
    .en(1'b1), .reset(or_1_out));
  and and_3 (and_3_out, Set, ~Input_Address[1]);  // AND_Gate
  and and_4 (and_4_out, Set, Input_Address[2]);
  and and_5 (and_5_out, Set, Input_Address[1]);
  or or_2 (or_2_out, Reset, and_3_out);
  J_K_Flip_Flop j_k_ff_2 (
    .J(1'b1), .clk(j_k_ff_1_qn), .K(1'b1), .Q(Output_Address[1]), .Qn(j_k_ff_2_qn), .preset(and_5_out),
    .en(1'b1), .reset(or_2_out));
  and and_6 (and_6_out, Set, ~Input_Address[2]);  // AND_Gate
  and and_7 (and_7_out, Set, Input_Address[3]);
  or or_3 (or_3_out, Reset, and_6_out);
  J_K_Flip_Flop j_k_ff_3 (
    .J(1'b1), .clk(j_k_ff_2_qn), .K(1'b1), .Q(Output_Address[2]), .Qn(j_k_ff_3_qn), .preset(and_4_out),
    .en(1'b1), .reset(or_3_out));
  and and_8 (and_8_out, Set, ~Input_Address[3]);  // AND_Gate
  and and_9 (and_9_out, Set, Input_Address[4]);
  or or_4 (or_4_out, Reset, and_12_out);
  or or_5 (or_5_out, Reset, and_8_out);
  J_K_Flip_Flop j_k_ff_4 (
    .J(1'b1), .clk(j_k_ff_3_qn), .K(1'b1), .Q(Output_Address[3]), .Qn(j_k_ff_4_qn), .preset(and_7_out),
    .en(1'b1), .reset(or_5_out));
  and and_10 (and_10_out, Set, Input_Address[5]);
  and and_11 (and_11_out, Set, ~Input_Address[5]);  // AND_Gate
  and and_12 (and_12_out, Set, ~Input_Address[4]);  // AND_Gate
  or or_6 (or_6_out, Reset, and_11_out);
  and and_13 (and_13_out, Set, ~Input_Address[6]);  // AND_Gate
  and and_14 (and_14_out, Set, Input_Address[6]);
  or or_7 (or_7_out, Reset, and_13_out);
  J_K_Flip_Flop j_k_ff_5 (
    .J(1'b1), .clk(j_k_ff_4_qn), .K(1'b1), .Q(Output_Address[4]), .Qn(j_k_ff_5_qn), .preset(and_9_out),
    .en(1'b1), .reset(or_4_out));
  and and_15 (and_15_out, Set, ~Input_Address[7]);  // AND_Gate
  and and_16 (and_16_out, Set, Input_Address[7]);
  or or_8 (or_8_out, Reset, and_15_out);
  J_K_Flip_Flop j_k_ff_6 (
    .J(1'b1), .clk(j_k_ff_5_qn), .K(1'b1), .Q(Output_Address[5]), .Qn(j_k_ff_6_qn), .preset(and_10_out),
    .en(1'b1), .reset(or_6_out));
  J_K_Flip_Flop j_k_ff_7 (
    .J(1'b1), .clk(j_k_ff_6_qn), .K(1'b1), .Q(Output_Address[6]), .Qn(j_k_ff_7_qn), .preset(and_14_out),
    .en(1'b1), .reset(or_7_out));
  J_K_Flip_Flop j_k_ff_8 (
    .J(1'b1), .clk(j_k_ff_7_qn), .K(1'b1), .Q(Output_Address[7]), .preset(and_16_out), .en(1'b1),
    .reset(or_8_out));  // open: Qn
endmodule

module ACC (
  input  [15:0] Input,
  input  Set,
  input  Reset,
  output [15:0] Output
);

  Register #(.width(16)) register_1 (.D(Input), .en(1'b1), .Q(Output), .clk(Set), .clr(Reset));
endmodule

module IR (
  input  [7:0] \Endereço ,
  input  Set,
  input  Reset,
  input  [7:0] \Código ,
  output [15:0] Output
);

  Register register_1 (.D(\Endereço ), .en(1'b1), .Q(Output[7:0]), .clk(Set), .clr(Reset));
  Register register_2 (.D(\Código ), .en(1'b1), .Q(Output[15:8]), .clk(Set), .clr(Reset));
endmodule

module CTRL (
  input  [15:0] RAM_OUT,
  input  [7:0] PC_Address_OUT,
  input  [15:0] ACC_OUT,
  input  [15:0] IR_OUT,
  output RAM_CLR,
  output ACC_SET,
  output ACC_RESET,
  output [15:0] ACC_IN,
  output PC_SET,
  output IR_SET,
  output PC_RESET,
  output IR_RESET,
  output PC_CU,
  output [7:0] IR_Address,
  output [7:0] PC_Address_IN,
  output [7:0] IR_Codigo,
  output RAM_LD
);

  wire clock_1_out;

  Clock clock_1 (.out(clock_1_out));
endmodule

module teste2 (
  input  in_1,
  input  in_2,
  input  in_3,
  input  in_4,
  input  [7:0] in_5,
  input  [15:0] in_6,
  input  in_7,
  input  in_8,
  input  in_9,
  output [15:0] out_10
);

  wire [7:0] pc_1_output_address, undriven;
  wire [15:0] ir_1_output, ram_1_data;

  CTRL ctrl_1 ();  // open: RAM_OUT, RAM_CLR, PC_SET, PC_RESET, PC_CU, PC_Address_IN, ACC_SET, ACC_RESET, ACC_IN, IR_SET, IR_RESET, IR_Address, IR_Codigo, PC_Address_OUT, ACC_OUT, IR_OUT, RAM_LD
  RAM #(.dataWidth(16)) ram_1 (
    .addr(pc_1_output_address), .data(ram_1_data), .sel(in_7), .clk(in_8), .ld(in_9));  // open: clr
  PC pc_1 (
    .Reset(in_3), .Counter_UP(in_2), .Input_Address(undriven), .Output_Address(pc_1_output_address));  // open: Set
  ACC acc_1 ();  // open: Input, Output, Set, Reset
  SPL168 spl168_1 (.in_1(ram_1_data));  // open: out_2, out_3
  IR ir_1 (.Set(in_2), .Reset(in_1), .Output(ir_1_output));  // open: Endereço, Código
  SPL168 spl168_2 ();  // open: in_1, out_2, out_3
endmodule

module SPL168 (
  input  [15:0] in_1,
  output [7:0] out_2,
  output [7:0] out_3
);


  assign out_2 = in_1[7:0];
  assign out_3 = in_1[15:8];
endmodule
