// Logisim project EP3.circ as structural Verilog: 4 circuits, main circuit main
module PC (
  input  [7:0] Input_Address,
  input  Set,
  input  Reset,
  input  Counter_UP,
  output [7:0] Output_Address
);

  wire and_1_out, and_2_out, and_3_out, and_4_out, and_5_out, and_6_out, and_7_out, and_8_out, and_9_out,
       and_10_out, and_11_out, and_12_out, and_13_out, and_14_out, and_15_out, and_16_out, j_k_ff_1_qn,
       j_k_ff_2_qn, j_k_ff_3_qn, j_k_ff_4_qn, j_k_ff_5_qn, j_k_ff_6_qn, j_k_ff_7_qn, or_1_out, or_2_out,
       or_3_out, or_4_out, or_5_out, or_6_out, or_7_out, or_8_out;

  and and_1 (and_1_out, Set, Input_Address[0]);
  J_K_Flip_Flop j_k_ff_1 (
    .J(1'b1), .clk(Counter_UP), .K(1'b1), .Q(Output_Address[0]), .Qn(j_k_ff_1_qn), .preset(and_1_out),
    .en(1'b1), .reset(or_1_out));
  and and_2 (and_2_out, Set, Input_Address[1]);
  and and_3 (and_3_out, Set, ~Input_Address[0]);  // AND_Gate
  or or_1 (or_1_out, Reset, and_3_out);
  or or_2 (or_2_out, Reset, and_5_out);
  J_K_Flip_Flop j_k_ff_2 (
    .J(1'b1), .clk(j_k_ff_1_qn), .K(1'b1), .Q(Output_Address[1]), .Qn(j_k_ff_2_qn), .preset(and_2_out),
    .en(1'b1), .reset(or_2_out));
  and and_4 (and_4_out, Set, ~Input_Address[2]);  // AND_Gate
  and and_5 (and_5_out, Set, ~Input_Address[1]);  // AND_Gate
  and and_6 (and_6_out, Set, Input_Address[2]);
  or or_3 (or_3_out, Reset, and_4_out);
  and and_7 (and_7_out, Set, ~Input_Address[3]);  // AND_Gate
  and and_8 (and_8_out, Set, Input_Address[3]);
  or or_4 (or_4_out, Reset, and_7_out);
  J_K_Flip_Flop j_k_ff_3 (
    .J(1'b1), .clk(j_k_ff_2_qn), .K(1'b1), .Q(Output_Address[2]), .Qn(j_k_ff_3_qn), .preset(and_6_out),
    .en(1'b1), .reset(or_3_out));
  and and_9 (and_9_out, Set, ~Input_Address[4]);  // AND_Gate
  and and_10 (and_10_out, Set, Input_Address[4]);
  or or_5 (or_5_out, Reset, and_9_out);
  J_K_Flip_Flop j_k_ff_4 (
    .J(1'b1), .clk(j_k_ff_3_qn), .K(1'b1), .Q(Output_Address[3]), .Qn(j_k_ff_4_qn), .preset(and_8_out),
    .en(1'b1), .reset(or_4_out));
  and and_11 (and_11_out, Set, Input_Address[5]);
  and and_12 (and_12_out, Set, ~Input_Address[5]);  // AND_Gate
  or or_6 (or_6_out, Reset, and_12_out);
  J_K_Flip_Flop j_k_ff_5 (
    .J(1'b1), .clk(j_k_ff_4_qn), .K(1'b1), .Q(Output_Address[4]), .Qn(j_k_ff_5_qn), .preset(and_10_out),
    .en(1'b1), .reset(or_5_out));
  and and_13 (and_13_out, Set, Input_Address[6]);
  and and_14 (and_14_out, Set, Input_Address[7]);
  and and_15 (and_15_out, Set, ~Input_Address[6]);  // AND_Gate
  or or_7 (or_7_out, Reset, and_15_out);
  J_K_Flip_Flop j_k_ff_6 (
    .J(1'b1), .clk(j_k_ff_5_qn), .K(1'b1), .Q(Output_Address[5]), .Qn(j_k_ff_6_qn), .preset(and_11_out),
    .en(1'b1), .reset(or_6_out));
  and and_16 (and_16_out, Set, ~Input_Address[7]);  // AND_Gate
  or or_8 (or_8_out, Reset, and_16_out);
  J_K_Flip_Flop j_k_ff_7 (
    .J(1'b1), .clk(j_k_ff_6_qn), .K(1'b1), .Q(Output_Address[6]), .Qn(j_k_ff_7_qn), .preset(and_13_out),
    .en(1'b1), .reset(or_7_out));
  J_K_Flip_Flop j_k_ff_8 (
    .J(1'b1), .clk(j_k_ff_7_qn), .K(1'b1), .Q(Output_Address[7]), .preset(and_14_out), .en(1'b1),
    .reset(or_8_out));  // open: Qn
endmodule

module CTRL (
  input  Entradas,
  input  in_2,
  input  [15:0] IR_OUT,
  input  [7:0] in_4,
  output RAM_CLOCK,
  output RAM_LD,
  output CU,
  output IR_EN,
  output ACC_EN,
  output PC_SET,
  output [7:0] PC_IN,
  output [7:0] RAM_ADDRESS
);

  wire and_1_out, clock_1_out, ENABLE, NOP, or_1_out, STA, STOP;
  wire [1:0] counter_1_q;

  and and_1 (and_1_out, ~STOP, Entradas);  // AND_Gate
  Demultiplexer #(.select(2), .enable("false")) demultiplexer_1 (
    .out0(IR_EN), .out1(CU), .out2(ENABLE), .in(1'b1), .sel(counter_1_q));  // open: out3
  Counter #(.width(2), .max('h2)) counter_1 (
    .Q(counter_1_q), .clk(and_1_out), .clr(in_2));  // open: load, D, count, carry
  Clock clock_1 (.out(clock_1_out));
  Transistor #(.\type ("n")) transistor_1 (.in(clock_1_out), .out(RAM_CLOCK), .gate(ENABLE));
  CMP cmp_1 (.in_1(IR_OUT[7:0]), .in_2(8'hb), .out_4(ACC_EN), .Enable(ENABLE));
  CMP cmp_2 (.in_1(IR_OUT[7:0]), .in_2(8'h32), .out_4(NOP), .Enable(ENABLE));
  CMP cmp_3 (.in_1(IR_OUT[7:0]), .in_2(8'h46), .out_4(STOP), .Enable(ENABLE));
  CMP cmp_4 (.in_1(IR_OUT[7:0]), .in_2(8'hc), .out_4(STA), .Enable(ENABLE));
  CMP cmp_5 (.in_1(IR_OUT[7:0]), .in_2(8'h33), .out_4(PC_SET), .Enable(ENABLE));
  or or_1 (or_1_out, ACC_EN, STA);
  Transistor #(.width(8)) transistor_2 (.in(in_4), .out(RAM_ADDRESS), .gate(or_1_out));
  Transistor #(.\type ("n"), .width(8)) transistor_3 (.in(IR_OUT[15:8]), .out(RAM_ADDRESS), .gate(or_1_out));
  not not_1 (RAM_LD, STA);

  assign PC_IN = IR_OUT[15:8];

  // Other names for the same wires on the sheet: CLOCK = Entradas; COD[7:0] = IR_OUT[7:0];
  //   IR_ADDR[7:0] = IR_OUT[15:8]; JMP = PC_SET; LDA = ACC_EN; PC_OUT[7:0] = in_4; RESET = in_2

  // Notes on the sheet:
  //   Ciclo de Instrução
  //   LDA - 11
  //   NOP - 50
  //   STP - 70
  //   Instruções
  //   STA - 12
  //   JMP - 51
  //   Selecionar acesso à RAM
  //   Saídas
endmodule

module CMP (
  input  [7:0] in_1,
  input  [7:0] in_2,
  input  Enable,
  output out_4
);

  wire and_1_out;
  wire [7:0] xnor_1_out;

  assign xnor_1_out = ~(in_1 ^ in_2);  // XNOR_Gate xnor_1, 8 bits wide
  and and_1 (and_1_out, xnor_1_out[0], xnor_1_out[1], xnor_1_out[2], xnor_1_out[3], xnor_1_out[4], xnor_1_out[5], xnor_1_out[6], xnor_1_out[7]);
  and and_2 (out_4, and_1_out, Enable);
endmodule

module main (
);

  wire ACC_EN, CLOCK, CU, IR_EN, PC_SET, RAM_CLOCK, RAM_LOAD, RESET;
  wire [7:0] PC_IN, PC_OUT, RAM_ADDR;
  wire [15:0] ACC_OUT, IR_OUT, RAM_OUT, transistor_1_out;

  Button button_1 (.out(RESET));
  Clock #(.highDuration(2)) clock_1 (.out(CLOCK));
  CTRL ctrl_1 (
    .IR_OUT(IR_OUT), .RAM_LD(RAM_LOAD), .IR_EN(IR_EN), .CU(CU), .RAM_CLOCK(RAM_CLOCK), .Entradas(CLOCK),
    .in_2(RESET), .PC_IN(PC_IN), .PC_SET(PC_SET), .RAM_ADDRESS(RAM_ADDR), .in_4(PC_OUT), .ACC_EN(ACC_EN));
  Transistor #(.width(16)) transistor_1 (.in(ACC_OUT), .out(transistor_1_out), .gate(RAM_LOAD));
  RAM #(.dataWidth(16)) ram_1 (
    .addr(RAM_ADDR), .data(transistor_1_out), .sel(1'b1), .clk(RAM_CLOCK), .ld(RAM_LOAD));  // open: clr
  Transistor #(.\type ("n"), .width(16)) transistor_2 (.in(transistor_1_out), .out(RAM_OUT), .gate(RAM_LOAD));
  Register #(.width(16)) ACC (.D(RAM_OUT), .en(ACC_EN), .Q(ACC_OUT), .clk(CLOCK), .clr(RESET));
  Register #(.width(16)) IR (.D(RAM_OUT), .en(IR_EN), .Q(IR_OUT), .clk(CLOCK), .clr(RESET));
  PC pc_1 (.Set(PC_SET), .Reset(RESET), .Counter_UP(CU), .Input_Address(PC_IN), .Output_Address(PC_OUT));

  // Notes on the sheet:
  //   Início
  //   RAM
endmodule
